# Fritzing sketch MainNode_final (saved by Fritzing 0.9.9b)
breadboards: 1

parts:
  Mod1 = Amica NodeMCU DEVKIT 1.0
  Part1 = NeoPixel NeoMatrix 8x8 [part_number=1487]
  R1 = Resistor [tolerance=±5% power=0.25 resistance=330 package=THT]
  DHT1 = DHT11 Humitidy and Temperature Sensor
  R2 = Resistor [tolerance=±5% power=0.25 resistance=10k package=THT]
  PMS5003 = mystery part, 8 pins [chip_label=PMS5003]

nets:
  GND: Mod1.pin2, Mod1.pin_9, Mod1.pin_29, Part1.GND, DHT1.GND, PMS5003.pin2
  N1: Mod1.pin7, PMS5003.pin3
  N2: Mod1.pin8, DHT1.DATA, R2.Pin_1
  N3: Mod1.pin_10, Mod1.pin_26, DHT1.VDD, R2.Pin_0
  N4: Mod1.pin_13, PMS5003.pin5
  N5: Mod1.pin_14, R1.Pin_0
  N6: Mod1.pin_30, Part1.VDD, PMS5003.pin1
  N7: Part1.IN, R1.Pin_1

notes:
  Output to led matrix
  PMS5003
  5v (1)
  Gnd (2)
  SET (3)
  - LOW level puts device in sleeping mode
  - HIGH for normal operation
  RX (4)
  TX (5)
  RESET (6) reset on LOW
  NC(7,8)
  NeoPixel 8x8
  Data In (1)
  5V (2)
  Gnd (3)

custom parts:
  NeoPixel NeoMatrix 8x8: Put on your sunglasses before wiring up this LED matrix - 64 eye-blistering RGB LEDs adorn the NeoMatrix for a blast of configurable color. Arranged in an 8x8 matrix, each pixel is individually addressable. Only one microcontroller pin is required to control all the LEDs, and you get 24 bit color for each LED.
  DHT11 Humitidy and Temperature Sensor: DHT11 Humidity and Temperature Sensor
