# Fritzing sketch SenseNode_final (saved by Fritzing 0.9.9b)
breadboards: 1

parts:
  Mod1 = Amica NodeMCU DEVKIT 1.0
  DHT1 = DHT11 Humitidy and Temperature Sensor
  R2 = Resistor [tolerance=±5% power=0.25 resistance=10k package=THT]
  Part1 = Adafruit CCS811
  LED1 = RGB LED (com. cathode, rbg) [package="5 mm [THT]"]
  R3 = Resistor [tolerance=±5% power=0.25 resistance=220 package=THT]
  R4 = Resistor [tolerance=±5% power=0.25 resistance=220 package=THT]
  R5 = Resistor [tolerance=±5% power=0.25 resistance=220 package=THT]

nets:
  VDD: Mod1.pin1, Mod1.pin_10, Mod1.pin_26, DHT1.VDD, R2.Pin_0, Part1.VIN
  GND: Mod1.pin2, DHT1.GND, Part1.GND, Part1.!WAKE, LED1.common_cathode
  N1: Mod1.pin6, DHT1.DATA, R2.Pin_1
  N2: Mod1.pin7, Part1.SDA
  N3: Mod1.pin8, Part1.SCL
  N4: Mod1.pin_11, R5.Pin_0
  N5: Mod1.pin_13, R3.Pin_0
  N6: Mod1.pin_14, R4.Pin_0
  N7: LED1.red_anode, R3.Pin_1
  N8: LED1.blue_anode, R4.Pin_1
  N9: LED1.green_anode, R5.Pin_1

custom parts:
  DHT11 Humitidy and Temperature Sensor: DHT11 Humidity and Temperature Sensor
